// Logisim project Adders_onwards.circ as structural Verilog: 31 circuits, main circuit notMain
module main (
  input  Counter_OE,
  input  Count_enable,
  input  WE_MAR_A,
  input  OE_MAR_A,
  input  [15:0] Testing_Data,
  input  WE_MAR_B,
  input  OE_Testing_Data,
  input  OR_MAR_B,
  input  Internal_OE,
  input  WE_IR,
  input  OE_IR,
  input  WE_MBR_A,
  input  OE_MBR_A,
  input  WE_MBR_B,
  input  OE_MBR_B,
  input  WE_R1,
  input  [3:0] Signal_ALU,
  input  WE_OUT,
  input  OE_ALU,
  input  OE_OUT,
  input  WE_R2,
  output [4:0] MAR_A_Content,
  output [4:0] Content_of_counter,
  output [4:0] MAR_B_Content,
  output [15:0] IR_Content,
  output [15:0] MBR_A_Content,
  output [15:0] MBR_B_Content,
  output [15:0] Reg_A_Content,
  output [15:0] ALU_Result,
  output [15:0] Output_Content,
  output [15:0] Reg_B_Content
);

  wire clock_CPU_out;
  wire [4:0] controlled_buffer_1_out, mar_1_dout;
  wire [15:0] alu_1_decision, Instruction_Register_dout;

  Clock clock_CPU (.out(clock_CPU_out));
  Counter #(.max('h10), .width(5)) Program_Counter (
    .up(Count_enable), .clk(clock_CPU_out), .D(controlled_buffer_1_out), .Q(Content_of_counter));  // open: clr, load, count, carry
  assign controlled_buffer_1_out = Counter_OE ? Content_of_counter : 5'bz;  // Controlled_Buffer controlled_buffer_1
  // Probe on Content_of_counter
  Register_Circuit Instruction_Register (
    .Clock(clock_CPU_out), .WE(WE_IR), .OE(OE_IR), .Din(alu_1_decision), .Dout(Instruction_Register_dout),
    .Stored_Data(IR_Content));
  Register_Circuit Register_1 (
    .Clock(clock_CPU_out), .WE(WE_R1), .Din(alu_1_decision), .Stored_Data(Reg_A_Content));  // open: OE, Dout
  Register_Circuit Register_2 (
    .Clock(clock_CPU_out), .WE(WE_R2), .Din(alu_1_decision), .Stored_Data(Reg_B_Content));  // open: OE, Dout
  // Probe on Reg_A_Content
  // Probe on Reg_B_Content
  BitSelector #(.group(5), .width(16)) bitselector_1 (
    .in(Instruction_Register_dout), .out(controlled_buffer_1_out), .sel(2'b00));
  // Probe on ALU_Result
  ALU alu_1 (
    .A(Reg_A_Content), .B(Reg_B_Content), .S(Signal_ALU), .OE(OE_ALU), .Dout(ALU_Result),
    .Decision(alu_1_decision));  // open: Flag, Carry_overflow, HALT
  // Probe on Testing_Data
  LED D15 (.in(alu_1_decision[15]));
  LED D14 (.in(alu_1_decision[14]));
  LED D13 (.in(alu_1_decision[13]));
  LED D9 (.in(alu_1_decision[9]));
  LED D12 (.in(alu_1_decision[12]));
  LED D10 (.in(alu_1_decision[10]));
  LED D11 (.in(alu_1_decision[11]));
  assign alu_1_decision = OE_Testing_Data ? Testing_Data : 16'bz;  // Controlled_Buffer controlled_buffer_2
  LED D8 (.in(alu_1_decision[8]));
  LED D7 (.in(alu_1_decision[7]));
  LED D6 (.in(alu_1_decision[6]));
  LED D5 (.in(alu_1_decision[5]));
  LED D4 (.in(alu_1_decision[4]));
  LED D3 (.in(alu_1_decision[3]));
  LED D2 (.in(alu_1_decision[2]));
  LED D1 (.in(alu_1_decision[1]));
  LED D0 (.in(alu_1_decision[0]));
  assign alu_1_decision = Internal_OE ? MBR_A_Content : 16'bz;  // Controlled_Buffer controlled_buffer_3
  MAR mar_1 (
    .Clock(clock_CPU_out), .WE(WE_MAR_A), .Din(controlled_buffer_1_out), .OE(OE_MAR_A), .Dout(mar_1_dout),
    .Stored_Data(MAR_A_Content));
  MAR mar_2 (
    .Clock(clock_CPU_out), .WE(WE_MAR_B), .Din(controlled_buffer_1_out), .OE(OR_MAR_B), .Dout(mar_1_dout),
    .Stored_Data(MAR_B_Content));
  MBR mbr_1 (
    .Clock(clock_CPU_out), .WE(WE_MBR_A), .OE(OE_MBR_A), .Din(alu_1_decision), .Dout(alu_1_decision),
    .Stored_Data(MBR_A_Content));
  MBR mbr_2 (
    .Clock(clock_CPU_out), .WE(WE_MBR_B), .OE(OE_MBR_B), .Din(alu_1_decision), .Dout(alu_1_decision),
    .Stored_Data(MBR_B_Content));
  Register_Circuit register_circuit_1 (
    .Clock(clock_CPU_out), .WE(WE_OUT), .OE(OE_OUT), .Din(alu_1_decision), .Dout(alu_1_decision),
    .Stored_Data(Output_Content));
  LED led_1 (.in(alu_1_decision[15]));
  LED led_2 (.in(alu_1_decision[14]));
  LED led_3 (.in(alu_1_decision[12]));
  LED led_4 (.in(alu_1_decision[13]));
  LED led_5 (.in(alu_1_decision[11]));
  LED led_6 (.in(alu_1_decision[9]));
  LED led_7 (.in(alu_1_decision[8]));
  LED led_8 (.in(alu_1_decision[7]));
  LED led_9 (.in(alu_1_decision[10]));
  LED led_10 (.in(alu_1_decision[6]));
  LED led_11 (.in(alu_1_decision[5]));
  LED led_12 (.in(alu_1_decision[4]));
  LED led_13 (.in(alu_1_decision[3]));
  LED led_14 (.in(alu_1_decision[2]));
  LED led_15 (.in(alu_1_decision[1]));
  LED led_16 (.in(alu_1_decision[0]));
  RAM #(.addrWidth(5), .dataWidth(16)) INST (.addr(mar_1_dout));  // open: we, oe, clk, din, dout
  RAM #(.addrWidth(16), .dataWidth(16)) Data_A (.addr(alu_1_decision));  // open: we, oe, clk, din, dout
  RAM #(.addrWidth(16), .dataWidth(16)) Data_B (.addr(alu_1_decision));  // open: we, oe, clk, din, dout
  RAM #(.addrWidth(5), .dataWidth(16)) System ();  // open: addr, we, oe, clk, din, dout
endmodule

module HalfAdder_2_bit (
  input  in_1,
  input  in_2
);

  wire and_1_out, xor_1_out;

  xor xor_1 (xor_1_out, in_1, in_2);
  and and_1 (and_1_out, in_1, in_2);
  LED led_1 (.in(xor_1_out));
  LED led_2 (.in(and_1_out));

  // Notes on the sheet:
  //   SUM
  //   Carry Out
endmodule

module FullAdder_2_bit (
  input  A,
  input  B,
  input  Carry_in,
  output sum,
  output Carry_out
);

  wire and_1_out, and_2_out, xor_1_out;

  xor xor_1 (xor_1_out, A, B);
  and and_1 (and_1_out, A, B);
  xor xor_2 (sum, xor_1_out, Carry_in);
  and and_2 (and_2_out, xor_1_out, Carry_in);
  LED led_1 (.in(xor_1_out));
  LED led_2 (.in(and_1_out));
  or or_1 (Carry_out, and_1_out, and_2_out);
  LED led_3 (.in(sum));
  LED led_4 (.in(Carry_out));

  // Notes on the sheet:
  //   Sum Intermediate
  //   Carry One
  //   Sum
  //   Carry Out
endmodule

module FullAdder_4_bit (
  input  Carry_in,
  input  [3:0] A,
  input  [3:0] B,
  output Carry_out,
  output [3:0] Sums
);

  wire fulladder_2_bit_1_carry_out, fulladder_2_bit_2_carry_out, fulladder_2_bit_3_carry_out;

  FullAdder_2_bit fulladder_2_bit_1 (
    .A(A[0]), .B(B[0]), .Carry_in(Carry_in), .sum(Sums[0]), .Carry_out(fulladder_2_bit_1_carry_out));
  FullAdder_2_bit fulladder_2_bit_2 (
    .A(A[1]), .B(B[1]), .Carry_in(fulladder_2_bit_1_carry_out), .sum(Sums[1]),
    .Carry_out(fulladder_2_bit_2_carry_out));
  FullAdder_2_bit fulladder_2_bit_3 (
    .A(A[2]), .B(B[2]), .Carry_in(fulladder_2_bit_2_carry_out), .sum(Sums[2]),
    .Carry_out(fulladder_2_bit_3_carry_out));
  // Probe on Sums
  FullAdder_2_bit fulladder_2_bit_4 (
    .A(A[3]), .B(B[3]), .Carry_in(fulladder_2_bit_3_carry_out), .sum(Sums[3]), .Carry_out(Carry_out));
endmodule

module FullAdder_16_bit (
  input  Carry_in,
  input  Sub,
  input  [15:0] A,
  input  [15:0] B,
  output [16:0] Negative,
  output Carry_out,
  output [15:0] Sums
);

  wire fulladder_4_bit_1_carry_out, fulladder_4_bit_2_carry_out, fulladder_4_bit_3_carry_out, or_1_out;
  wire [3:0] bit_extender_1_out, xor_1_out, xor_2_out, xor_3_out, xor_4_out;

  // Probe on A
  // Probe on B
  assign bit_extender_1_out = {{3{Sub}}, Sub};  // Bit_Extender bit_extender_1
  or or_1 (or_1_out, Carry_in, Sub);
  assign xor_1_out = B[3:0] ^ bit_extender_1_out;  // XOR_Gate xor_1, 4 bits wide
  assign xor_2_out = B[7:4] ^ bit_extender_1_out;  // XOR_Gate xor_2, 4 bits wide
  assign xor_3_out = B[11:8] ^ bit_extender_1_out;  // XOR_Gate xor_3, 4 bits wide
  assign xor_4_out = B[15:12] ^ bit_extender_1_out;  // XOR_Gate xor_4, 4 bits wide
  FullAdder_4_bit fulladder_4_bit_1 (
    .Carry_in(or_1_out), .A(A[3:0]), .B(xor_1_out), .Carry_out(fulladder_4_bit_1_carry_out),
    .Sums(Negative[3:0]));
  FullAdder_4_bit fulladder_4_bit_2 (
    .Carry_in(fulladder_4_bit_1_carry_out), .A(A[7:4]), .B(xor_2_out),
    .Carry_out(fulladder_4_bit_2_carry_out), .Sums(Negative[7:4]));
  FullAdder_4_bit fulladder_4_bit_3 (
    .Carry_in(fulladder_4_bit_2_carry_out), .A(A[11:8]), .B(xor_3_out),
    .Carry_out(fulladder_4_bit_3_carry_out), .Sums(Negative[11:8]));
  // Probe on Negative[15:0]
  // Probe on {Carry_out, Negative[15:0]}
  FullAdder_4_bit fulladder_4_bit_4 (
    .Carry_in(fulladder_4_bit_3_carry_out), .A(xor_4_out), .B(A[15:12]), .Carry_out(Carry_out),
    .Sums(Negative[15:12]));

  assign Negative[16] = Carry_out;
  assign Sums = Negative[15:0];
endmodule

module Comparator_16_bit (
  input  [15:0] A,
  input  [15:0] B,
  output A_G_B,
  output A_E_B,
  output A_L_B
);

  wire comparator_4_bit_1_a_e_b, comparator_4_bit_1_a_g_b, comparator_4_bit_1_a_l_b,
       comparator_4_bit_2_a_e_b, comparator_4_bit_2_a_g_b, comparator_4_bit_2_a_l_b,
       comparator_4_bit_3_a_e_b, comparator_4_bit_3_a_g_b, comparator_4_bit_3_a_l_b;

  Comparator_4_bit comparator_4_bit_1 (
    .A(A[15:12]), .B(B[15:12]), .A_greater_B(1'b0), .A_equals_B(1'b1), .A_lesser_B(1'b0),
    .A_G_B(comparator_4_bit_1_a_g_b), .A_E_B(comparator_4_bit_1_a_e_b), .A_L_B(comparator_4_bit_1_a_l_b));
  Comparator_4_bit comparator_4_bit_2 (
    .A(A[7:4]), .B(B[7:4]), .A_greater_B(comparator_4_bit_3_a_g_b), .A_equals_B(comparator_4_bit_3_a_e_b),
    .A_lesser_B(comparator_4_bit_3_a_l_b), .A_G_B(comparator_4_bit_2_a_g_b),
    .A_E_B(comparator_4_bit_2_a_e_b), .A_L_B(comparator_4_bit_2_a_l_b));
  Comparator_4_bit comparator_4_bit_3 (
    .A(A[11:8]), .B(B[11:8]), .A_greater_B(comparator_4_bit_1_a_g_b), .A_equals_B(comparator_4_bit_1_a_e_b),
    .A_lesser_B(comparator_4_bit_1_a_l_b), .A_G_B(comparator_4_bit_3_a_g_b),
    .A_E_B(comparator_4_bit_3_a_e_b), .A_L_B(comparator_4_bit_3_a_l_b));
  Comparator_4_bit comparator_4_bit_4 (
    .A(A[3:0]), .B(B[3:0]), .A_greater_B(comparator_4_bit_2_a_g_b), .A_equals_B(comparator_4_bit_2_a_e_b),
    .A_lesser_B(comparator_4_bit_2_a_l_b), .A_G_B(A_G_B), .A_E_B(A_E_B), .A_L_B(A_L_B));
endmodule

module Comparator_4_bit (
  input  [3:0] A,
  input  [3:0] B,
  input  A_greater_B,
  input  A_equals_B,
  input  A_lesser_B,
  output A_G_B,
  output A_E_B,
  output A_L_B
);

  wire and_1_out, and_2_out, and_3_out, and_4_out, and_5_out, and_6_out, and_7_out, and_8_out, and_9_out,
       and_10_out, and_11_out, not_1_out, not_2_out, not_3_out, not_4_out, not_5_out, not_6_out, not_7_out,
       not_8_out, or_1_out, or_2_out, xnor_1_out, xnor_2_out, xnor_3_out, xnor_4_out;

  xnor xnor_1 (xnor_1_out, A[3], B[3]);
  xnor xnor_2 (xnor_2_out, A[2], B[2]);
  xnor xnor_3 (xnor_3_out, A[1], B[1]);
  xnor xnor_4 (xnor_4_out, A[0], B[0]);
  not not_1 (not_1_out, B[3]);
  not not_2 (not_2_out, B[2]);
  not not_3 (not_3_out, B[1]);
  not not_4 (not_4_out, B[0]);
  not not_5 (not_5_out, A[0]);
  not not_6 (not_6_out, A[1]);
  not not_7 (not_7_out, A[2]);
  not not_8 (not_8_out, A[3]);
  and and_1 (and_1_out, A[3], not_1_out);
  and and_2 (and_2_out, A[2], xnor_1_out, not_2_out);
  and and_3 (and_3_out, A[1], xnor_1_out, xnor_2_out, not_3_out);
  and and_4 (and_4_out, A[0], xnor_1_out, xnor_2_out, xnor_3_out, not_4_out);
  and and_5 (and_5_out, B[3], not_8_out);
  and and_6 (and_6_out, B[2], xnor_1_out, not_7_out);
  and and_7 (and_7_out, B[1], xnor_1_out, xnor_2_out, not_6_out);
  and and_8 (and_8_out, B[0], xnor_1_out, xnor_2_out, xnor_3_out, not_5_out);
  or or_1 (or_1_out, and_1_out, and_2_out, and_3_out, and_4_out);
  and and_9 (and_9_out, xnor_1_out, xnor_2_out, xnor_3_out, xnor_4_out);
  or or_2 (or_2_out, and_5_out, and_6_out, and_7_out, and_8_out);
  and and_10 (and_10_out, A_equals_B, or_1_out);
  and and_11 (and_11_out, A_equals_B, or_2_out);
  or or_3 (A_G_B, and_10_out, A_greater_B);
  and and_12 (A_E_B, and_9_out, A_equals_B);
  or or_4 (A_L_B, and_11_out, A_lesser_B);

  // Notes on the sheet:
  //   A > B
  //   A = B
  //   A < B
endmodule

module MAR (
  input  Clock,
  input  WE,
  input  [4:0] Din,
  input  OE,
  output [4:0] Dout,
  output [4:0] Stored_Data
);

  Memory_Cell memory_cell_1 (
    .Clock(Clock), .WE(WE), .Din(Din[0]), .OE(OE), .Dout(Dout[0]), .Stored_Data(Stored_Data[0]));  // open: Reset
  Memory_Cell memory_cell_2 (
    .Clock(Clock), .WE(WE), .Din(Din[1]), .OE(OE), .Dout(Dout[1]), .Stored_Data(Stored_Data[1]));  // open: Reset
  Memory_Cell memory_cell_3 (
    .Clock(Clock), .WE(WE), .Din(Din[2]), .OE(OE), .Dout(Dout[2]), .Stored_Data(Stored_Data[2]));  // open: Reset
  Memory_Cell memory_cell_4 (
    .Clock(Clock), .WE(WE), .Din(Din[3]), .OE(OE), .Dout(Dout[3]), .Stored_Data(Stored_Data[3]));  // open: Reset
  Memory_Cell memory_cell_5 (
    .Clock(Clock), .WE(WE), .Din(Din[4]), .OE(OE), .Dout(Dout[4]), .Stored_Data(Stored_Data[4]));  // open: Reset
endmodule

module Memory_Cell (
  input  Clock,
  input  WE,
  input  Din,
  input  OE,
  input  Reset,
  output Dout,
  output Stored_Data
);

  wire and_1_out, and_2_out, not_1_out, or_1_out;

  not not_1 (not_1_out, WE);
  and and_1 (and_1_out, Stored_Data, not_1_out);
  and and_2 (and_2_out, WE, Din);
  or or_1 (or_1_out, and_1_out, and_2_out);
  D_Flip_Flop d_ff_1 (.D(or_1_out), .clk(Clock), .Q(Stored_Data), .reset(Reset));  // open: Qn, preset
  assign Dout = OE ? Stored_Data : 1'bz;  // Controlled_Buffer controlled_buffer_1
endmodule

module MBR (
  input  Clock,
  input  WE,
  input  OE,
  input  [15:0] Din,
  output [15:0] Dout,
  output [15:0] Stored_Data
);

  Memory_Cell memory_cell_1 (
    .Clock(Clock), .WE(WE), .Din(Din[0]), .OE(OE), .Dout(Dout[0]), .Stored_Data(Stored_Data[0]));  // open: Reset
  Memory_Cell memory_cell_2 (
    .Clock(Clock), .WE(WE), .Din(Din[1]), .OE(OE), .Dout(Dout[1]), .Stored_Data(Stored_Data[1]));  // open: Reset
  Memory_Cell memory_cell_3 (
    .WE(WE), .Din(Din[2]), .OE(OE), .Dout(Dout[2]), .Stored_Data(Stored_Data[2]));  // open: Clock, Reset
  Memory_Cell memory_cell_4 (
    .Clock(Clock), .WE(WE), .Din(Din[3]), .OE(OE), .Dout(Dout[3]), .Stored_Data(Stored_Data[3]));  // open: Reset
  Memory_Cell memory_cell_5 (
    .Clock(Clock), .WE(WE), .Din(Din[4]), .OE(OE), .Dout(Dout[4]), .Stored_Data(Stored_Data[4]));  // open: Reset
  Memory_Cell memory_cell_6 (
    .Clock(Clock), .WE(WE), .Din(Din[5]), .OE(OE), .Dout(Dout[5]), .Stored_Data(Stored_Data[5]));  // open: Reset
  Memory_Cell memory_cell_7 (
    .Clock(Clock), .WE(WE), .Din(Din[6]), .OE(OE), .Dout(Dout[6]), .Stored_Data(Stored_Data[6]));  // open: Reset
  Memory_Cell memory_cell_8 (
    .Clock(Clock), .WE(WE), .Din(Din[7]), .OE(OE), .Dout(Dout[7]), .Stored_Data(Stored_Data[7]));  // open: Reset
  Memory_Cell memory_cell_9 (
    .Clock(Clock), .WE(WE), .Din(Din[8]), .OE(OE), .Dout(Dout[8]), .Stored_Data(Stored_Data[8]));  // open: Reset
  Memory_Cell memory_cell_10 (
    .Clock(Clock), .WE(WE), .Din(Din[9]), .OE(OE), .Dout(Dout[9]), .Stored_Data(Stored_Data[9]));  // open: Reset
  Memory_Cell memory_cell_11 (
    .Clock(Clock), .WE(WE), .Din(Din[10]), .OE(OE), .Dout(Dout[10]), .Stored_Data(Stored_Data[10]));  // open: Reset
  Memory_Cell memory_cell_12 (
    .Clock(Clock), .WE(WE), .Din(Din[11]), .OE(OE), .Dout(Dout[11]), .Stored_Data(Stored_Data[11]));  // open: Reset
  Memory_Cell memory_cell_13 (
    .Clock(Clock), .WE(WE), .Din(Din[12]), .OE(OE), .Dout(Dout[12]), .Stored_Data(Stored_Data[12]));  // open: Reset
  Memory_Cell memory_cell_14 (
    .Clock(Clock), .WE(WE), .Din(Din[13]), .OE(OE), .Dout(Dout[13]), .Stored_Data(Stored_Data[13]));  // open: Reset
  Memory_Cell memory_cell_15 (
    .Clock(Clock), .WE(WE), .Din(Din[14]), .OE(OE), .Dout(Dout[14]), .Stored_Data(Stored_Data[14]));  // open: Reset
  Memory_Cell memory_cell_16 (
    .Clock(Clock), .WE(WE), .Din(Din[15]), .OE(OE), .Dout(Dout[15]), .Stored_Data(Stored_Data[15]));  // open: Reset
endmodule

module Multiplexer_4_to_1_4bits (
  input  [3:0] I_0,
  input  [3:0] I_1,
  input  [3:0] I_2,
  input  [3:0] I_3,
  input  S_0,
  input  S_1,
  output [3:0] Decision
);

  Multiplexer_4_to_1_1bit multiplexer_4_to_1_1bit_1 (
    .I_0(I_0[0]), .I_1(I_1[0]), .I_2(I_2[0]), .I_3(I_3[0]), .S_0(S_0), .S_1(S_1), .Decision(Decision[0]));
  Multiplexer_4_to_1_1bit multiplexer_4_to_1_1bit_2 (
    .I_0(I_0[1]), .I_1(I_1[1]), .I_2(I_2[1]), .I_3(I_3[1]), .S_0(S_0), .S_1(S_1), .Decision(Decision[1]));
  Multiplexer_4_to_1_1bit multiplexer_4_to_1_1bit_3 (
    .I_0(I_0[2]), .I_1(I_1[2]), .I_2(I_2[2]), .I_3(I_3[2]), .S_0(S_0), .S_1(S_1), .Decision(Decision[2]));
  Multiplexer_4_to_1_1bit multiplexer_4_to_1_1bit_4 (
    .I_0(I_0[3]), .I_1(I_1[3]), .I_2(I_2[3]), .I_3(I_3[3]), .S_0(S_0), .S_1(S_1), .Decision(Decision[3]));
endmodule

module Multiplexer_4_to_1_1bit (
  input  I_0,
  input  I_1,
  input  I_2,
  input  I_3,
  input  S_0,
  input  S_1,
  output Decision
);

  wire and_1_out, and_2_out, and_3_out, and_4_out, not_1_out, not_2_out;

  not not_1 (not_1_out, S_0);
  not not_2 (not_2_out, S_1);
  and and_1 (and_1_out, I_0, not_1_out, not_2_out);
  and and_2 (and_2_out, I_1, S_0, not_2_out);
  and and_3 (and_3_out, I_2, not_1_out, S_1);
  and and_4 (and_4_out, I_3, S_0, S_1);
  or or_1 (Decision, and_1_out, and_2_out, and_3_out, and_4_out);

  // Notes on the sheet:
  //   Decision: pull=down
endmodule

module Multiplexer_4_to_1_16bits (
  input  [15:0] I_0,
  input  [15:0] I_1,
  input  [15:0] I_2,
  input  [15:0] I_3,
  input  S_0,
  input  S_1,
  output [15:0] Decision
);

  Multiplexer_4_to_1_4bits multiplexer_4_to_1_4bits_1 (
    .I_0(I_0[3:0]), .I_1(I_1[3:0]), .I_2(I_2[3:0]), .I_3(I_3[3:0]), .S_0(S_0), .S_1(S_1),
    .Decision(Decision[3:0]));
  Multiplexer_4_to_1_4bits multiplexer_4_to_1_4bits_2 (
    .I_0(I_0[7:4]), .I_1(I_1[7:4]), .I_2(I_2[7:4]), .I_3(I_3[7:4]), .S_0(S_0), .S_1(S_1),
    .Decision(Decision[7:4]));
  Multiplexer_4_to_1_4bits multiplexer_4_to_1_4bits_3 (
    .I_0(I_0[11:8]), .I_1(I_1[11:8]), .I_2(I_2[11:8]), .I_3(I_3[11:8]), .S_0(S_0), .S_1(S_1),
    .Decision(Decision[11:8]));
  Multiplexer_4_to_1_4bits multiplexer_4_to_1_4bits_4 (
    .I_0(I_0[15:12]), .I_1(I_1[15:12]), .I_2(I_2[15:12]), .I_3(I_3[15:12]), .S_0(S_0), .S_1(S_1),
    .Decision(Decision[15:12]));
endmodule

module Multiplier_4_bits (
  input  [3:0] A,
  input  [3:0] B,
  output [7:0] Product
);

  wire [2:0] and_14_out;
  wire [3:0] and_4_out, and_8_out, and_12_out, fulladder_4_bit_2_carry_out, fulladder_4_bit_3_carry_out;

  // Probe on A
  and and_1 (and_4_out[3], A[3], B[3]);
  and and_2 (and_4_out[2], A[3], B[2]);
  and and_3 (and_4_out[1], A[3], B[1]);
  and and_4 (and_4_out[0], A[3], B[0]);
  and and_5 (and_8_out[3], A[2], B[3]);
  and and_6 (and_8_out[2], A[2], B[2]);
  and and_7 (and_8_out[1], A[2], B[1]);
  and and_8 (and_8_out[0], A[2], B[0]);
  // Probe on Product
  and and_9 (and_12_out[3], A[1], B[3]);
  and and_10 (and_12_out[2], A[1], B[2]);
  and and_11 (and_12_out[1], A[1], B[1]);
  FullAdder_4_bit fulladder_4_bit_1 (
    .Carry_in(1'b0), .A(fulladder_4_bit_2_carry_out), .B(and_4_out), .Carry_out(Product[7]),
    .Sums(Product[6:3]));
  // Probe on B
  and and_12 (and_12_out[0], A[1], B[0]);
  FullAdder_4_bit fulladder_4_bit_2 (
    .Carry_in(1'b0), .A(fulladder_4_bit_3_carry_out), .B(and_8_out),
    .Carry_out(fulladder_4_bit_2_carry_out[3]), .Sums({fulladder_4_bit_2_carry_out[2:0], Product[2]}));
  and and_13 (and_14_out[2], A[0], B[3]);
  FullAdder_4_bit fulladder_4_bit_3 (
    .Carry_in(1'b0), .A({1'b0, and_14_out}), .B(and_12_out), .Carry_out(fulladder_4_bit_3_carry_out[3]),
    .Sums({fulladder_4_bit_3_carry_out[2:0], Product[1]}));
  and and_14 (and_14_out[0], A[0], B[1]);
  and and_15 (and_14_out[1], A[0], B[2]);
  and and_16 (Product[0], A[0], B[0]);
endmodule

module Multiplier_16_bits (
  input  [7:0] A,
  input  [7:0] B,
  output Carry_Out,
  output [15:0] Product
);

  wire xor_1_out;
  wire [3:0] undriven_2, undriven_3, undriven_4, undriven_5;
  wire [7:0] multiplier_4_bits_1_product, multiplier_4_bits_2_product, multiplier_4_bits_3_product,
       multiplier_4_bits_4_product, undriven, undriven_6;
  wire [15:0] fulladder_16_bit_1_sums, fulladder_16_bit_2_sums;

  // Probe on A
  // Probe on B
  // Probe on A[7:4]
  // Probe on B[3:0]
  // Probe on B[7:4]
  // Probe on A[3:0]
  // Probe on multiplier_4_bits_1_product
  Multiplier_4_bits multiplier_4_bits_1 (.A(A[3:0]), .B(B[3:0]), .Product(multiplier_4_bits_1_product));
  Multiplier_4_bits multiplier_4_bits_2 (.A(A[3:0]), .B(B[7:4]), .Product(multiplier_4_bits_2_product));
  // Probe on multiplier_4_bits_2_product
  // Probe on multiplier_4_bits_3_product
  Multiplier_4_bits multiplier_4_bits_3 (.A(A[7:4]), .B(B[3:0]), .Product(multiplier_4_bits_3_product));
  Multiplier_4_bits multiplier_4_bits_4 (.A(A[7:4]), .B(B[7:4]), .Product(multiplier_4_bits_4_product));
  // Probe on multiplier_4_bits_4_product
  xor xor_1 (xor_1_out, A[7], B[7]);
  // Probe on fulladder_16_bit_1_sums
  FullAdder_16_bit fulladder_16_bit_1 (
    .A({undriven, multiplier_4_bits_1_product}), .B({undriven_3, multiplier_4_bits_2_product, undriven_2}),
    .Sums(fulladder_16_bit_1_sums));  // open: Carry_in, Sub, Negative, Carry_out
  FullAdder_16_bit fulladder_16_bit_2 (
    .A({undriven_5, multiplier_4_bits_3_product, undriven_4}), .B({multiplier_4_bits_4_product, undriven_6}),
    .Sums(fulladder_16_bit_2_sums));  // open: Carry_in, Sub, Negative, Carry_out
  // Probe on fulladder_16_bit_2_sums
  FullAdder_16_bit fulladder_16_bit_3 (
    .Sub(xor_1_out), .A(fulladder_16_bit_1_sums), .B(fulladder_16_bit_2_sums), .Carry_out(Carry_Out),
    .Sums(Product));  // open: Carry_in, Negative
  // Probe on Product
endmodule

module OR_Circuit (
  input  [15:0] A,
  input  [15:0] B,
  output [15:0] OR_Out
);

  // Probe on A
  // Probe on B
  assign OR_Out[3:0] = A[3:0] | B[3:0];  // OR_Gate or_1, 4 bits wide
  assign OR_Out[7:4] = A[7:4] | B[7:4];  // OR_Gate or_2, 4 bits wide
  assign OR_Out[11:8] = A[11:8] | B[11:8];  // OR_Gate or_3, 4 bits wide
  assign OR_Out[15:12] = A[15:12] | B[15:12];  // OR_Gate or_4, 4 bits wide
  // Probe on OR_Out
endmodule

module AND_Circuit (
  input  [15:0] A,
  input  [15:0] B,
  output [15:0] AND_Out
);

  // Probe on A
  // Probe on B
  assign AND_Out[3:0] = A[3:0] & B[3:0];  // AND_Gate and_1, 4 bits wide
  assign AND_Out[7:4] = A[7:4] & B[7:4];  // AND_Gate and_2, 4 bits wide
  assign AND_Out[11:8] = A[11:8] & B[11:8];  // AND_Gate and_3, 4 bits wide
  assign AND_Out[15:12] = A[15:12] & B[15:12];  // AND_Gate and_4, 4 bits wide
  // Probe on AND_Out
endmodule

module XOR_Circuit (
  input  [15:0] A,
  input  [15:0] B,
  output [15:0] XOR_Out
);

  // Probe on A
  // Probe on B
  assign XOR_Out[3:0] = A[3:0] ^ B[3:0];  // XOR_Gate xor_1, 4 bits wide
  assign XOR_Out[7:4] = A[7:4] ^ B[7:4];  // XOR_Gate xor_2, 4 bits wide
  assign XOR_Out[11:8] = A[11:8] ^ B[11:8];  // XOR_Gate xor_3, 4 bits wide
  assign XOR_Out[15:12] = A[15:12] ^ B[15:12];  // XOR_Gate xor_4, 4 bits wide
  // Probe on XOR_Out
endmodule

module NOT_Circuit (
  input  [15:0] A,
  output [15:0] NOT_Out
);

  // Probe on A
  not not_1 (NOT_Out[0], A[0]);
  not not_2 (NOT_Out[1], A[1]);
  not not_3 (NOT_Out[2], A[2]);
  not not_4 (NOT_Out[3], A[3]);
  not not_5 (NOT_Out[4], A[4]);
  not not_6 (NOT_Out[5], A[5]);
  not not_7 (NOT_Out[6], A[6]);
  not not_8 (NOT_Out[7], A[7]);
  not not_9 (NOT_Out[8], A[8]);
  not not_10 (NOT_Out[9], A[9]);
  not not_11 (NOT_Out[10], A[10]);
  not not_12 (NOT_Out[11], A[11]);
  not not_13 (NOT_Out[12], A[12]);
  not not_14 (NOT_Out[13], A[13]);
  not not_15 (NOT_Out[14], A[14]);
  not not_16 (NOT_Out[15], A[15]);
  // Probe on NOT_Out
endmodule

module Register_Circuit (
  input  Clock,
  input  WE,
  input  OE,
  input  [15:0] Din,
  output [15:0] Dout,
  output [15:0] Stored_Data
);

  Memory_Cell memory_cell_1 (
    .Clock(Clock), .WE(WE), .Din(Din[0]), .OE(OE), .Dout(Dout[0]), .Stored_Data(Stored_Data[0]));  // open: Reset
  Memory_Cell memory_cell_2 (
    .Clock(Clock), .WE(WE), .Din(Din[1]), .OE(OE), .Dout(Dout[1]), .Stored_Data(Stored_Data[1]));  // open: Reset
  Memory_Cell memory_cell_3 (
    .WE(WE), .Din(Din[2]), .OE(OE), .Dout(Dout[2]), .Stored_Data(Stored_Data[2]));  // open: Clock, Reset
  Memory_Cell memory_cell_4 (
    .Clock(Clock), .WE(WE), .Din(Din[3]), .OE(OE), .Dout(Dout[3]), .Stored_Data(Stored_Data[3]));  // open: Reset
  Memory_Cell memory_cell_5 (
    .Clock(Clock), .WE(WE), .Din(Din[4]), .OE(OE), .Dout(Dout[4]), .Stored_Data(Stored_Data[4]));  // open: Reset
  Memory_Cell memory_cell_6 (
    .Clock(Clock), .WE(WE), .Din(Din[5]), .OE(OE), .Dout(Dout[5]), .Stored_Data(Stored_Data[5]));  // open: Reset
  Memory_Cell memory_cell_7 (
    .Clock(Clock), .WE(WE), .Din(Din[6]), .OE(OE), .Dout(Dout[6]), .Stored_Data(Stored_Data[6]));  // open: Reset
  Memory_Cell memory_cell_8 (
    .Clock(Clock), .WE(WE), .Din(Din[7]), .OE(OE), .Dout(Dout[7]), .Stored_Data(Stored_Data[7]));  // open: Reset
  Memory_Cell memory_cell_9 (
    .Clock(Clock), .WE(WE), .Din(Din[8]), .OE(OE), .Dout(Dout[8]), .Stored_Data(Stored_Data[8]));  // open: Reset
  Memory_Cell memory_cell_10 (
    .Clock(Clock), .WE(WE), .Din(Din[9]), .OE(OE), .Dout(Dout[9]), .Stored_Data(Stored_Data[9]));  // open: Reset
  Memory_Cell memory_cell_11 (
    .Clock(Clock), .WE(WE), .Din(Din[10]), .OE(OE), .Dout(Dout[10]), .Stored_Data(Stored_Data[10]));  // open: Reset
  Memory_Cell memory_cell_12 (
    .Clock(Clock), .WE(WE), .Din(Din[11]), .OE(OE), .Dout(Dout[11]), .Stored_Data(Stored_Data[11]));  // open: Reset
  Memory_Cell memory_cell_13 (
    .Clock(Clock), .WE(WE), .Din(Din[12]), .OE(OE), .Dout(Dout[12]), .Stored_Data(Stored_Data[12]));  // open: Reset
  Memory_Cell memory_cell_14 (
    .Clock(Clock), .WE(WE), .Din(Din[13]), .OE(OE), .Dout(Dout[13]), .Stored_Data(Stored_Data[13]));  // open: Reset
  Memory_Cell memory_cell_15 (
    .Clock(Clock), .WE(WE), .Din(Din[14]), .OE(OE), .Dout(Dout[14]), .Stored_Data(Stored_Data[14]));  // open: Reset
  Memory_Cell memory_cell_16 (
    .Clock(Clock), .WE(WE), .Din(Din[15]), .OE(OE), .Dout(Dout[15]), .Stored_Data(Stored_Data[15]));  // open: Reset
endmodule

module Instruction_Splitter (
  input  [15:0] Instruction,
  input  WE,
  input  Clock,
  output [4:0] Address_B,
  output [4:0] Address_A,
  output [4:0] OP_Code,
  output Flag
);

  Register #(.width(16)) register_1 (
    .D(Instruction), .en(WE), .clk(Clock), .Q({Flag, OP_Code, Address_A, Address_B}));  // open: clr
endmodule

module ALU (
  input  [15:0] A,
  input  [15:0] B,
  input  Flag,
  input  [3:0] S,
  input  OE,
  output [15:0] Carry_overflow,
  output [15:0] Dout,
  output [15:0] Decision,
  output HALT
);

  wire comparator_4_bit_1_a_e_b, comparator_4_bit_2_a_e_b, comparator_16_bit_1_a_e_b,
       comparator_16_bit_1_a_g_b, comparator_16_bit_1_a_l_b, or_1_out;
  wire [0:0] fulladder_16_bit_1_carry_out, multiplier_16_bits_1_carry_out;
  wire [15:0] and_circuit_1_and_out, comparator_encoder_1_encoded, fulladder_16_bit_1_sums,
       multiplexer_4_to_1_16bits_1_decision, multiplexer_4_to_1_16bits_2_decision,
       multiplexer_4_to_1_16bits_3_decision, multiplexer_4_to_1_16bits_4_decision,
       multiplier_16_bits_1_product, not_circuit_1_not_out, undriven, xor_circuit_1_xor_out;

  // Probe on A
  // Probe on B
  FullAdder_16_bit fulladder_16_bit_1 (
    .Sub(Flag), .A(A), .B(B), .Carry_out(fulladder_16_bit_1_carry_out[0]), .Sums(fulladder_16_bit_1_sums));  // open: Carry_in, Negative
  // Probe on fulladder_16_bit_1_sums
  // Probe on multiplier_16_bits_1_product
  Multiplier_16_bits multiplier_16_bits_1 (
    .A(A[7:0]), .B(B[7:0]), .Carry_Out(multiplier_16_bits_1_carry_out[0]),
    .Product(multiplier_16_bits_1_product));
  Comparator_16_bit comparator_16_bit_1 (
    .A(A), .B(B), .A_G_B(comparator_16_bit_1_a_g_b), .A_E_B(comparator_16_bit_1_a_e_b),
    .A_L_B(comparator_16_bit_1_a_l_b));
  AND_Circuit and_circuit_1 (.A(A), .B(B), .AND_Out(and_circuit_1_and_out));
  XOR_Circuit xor_circuit_1 (.A(A), .B(B), .XOR_Out(xor_circuit_1_xor_out));
  NOT_Circuit not_circuit_1 (.A(A), .NOT_Out(not_circuit_1_not_out));
  OR_Circuit or_circuit_1 ();  // open: A, B, OR_Out
  Comparator_Encoder comparator_encoder_1 (
    .A_greater_B(comparator_16_bit_1_a_g_b), .A_equals_B(comparator_16_bit_1_a_e_b),
    .A_lesser_B(comparator_16_bit_1_a_l_b), .Encoded(comparator_encoder_1_encoded));
  // Probe on multiplexer_4_to_1_16bits_1_decision
  Multiplexer_4_to_1_16bits multiplexer_4_to_1_16bits_1 (
    .I_0(undriven), .I_1(fulladder_16_bit_1_sums), .I_3(multiplier_16_bits_1_product), .S_0(S[0]),
    .S_1(S[1]), .Decision(multiplexer_4_to_1_16bits_1_decision));  // open: I_2
  Multiplexer_4_to_1_16bits multiplexer_4_to_1_16bits_2 (
    .S_0(S[0]), .S_1(S[1]), .Decision(multiplexer_4_to_1_16bits_2_decision));  // open: I_0, I_1, I_2, I_3
  Multiplexer_4_to_1_16bits multiplexer_4_to_1_16bits_3 (
    .I_2(comparator_encoder_1_encoded), .I_3(and_circuit_1_and_out), .S_0(S[0]), .S_1(S[1]),
    .Decision(multiplexer_4_to_1_16bits_3_decision));  // open: I_0, I_1
  Multiplexer_4_to_1_16bits multiplexer_4_to_1_16bits_4 (
    .I_0(xor_circuit_1_xor_out), .I_1(not_circuit_1_not_out), .S_0(S[0]), .S_1(S[1]),
    .Decision(multiplexer_4_to_1_16bits_4_decision));  // open: I_2, I_3
  Comparator_4_bit comparator_4_bit_1 (
    .A(S), .B(4'b1110), .A_greater_B(1'b0), .A_equals_B(1'b1), .A_lesser_B(1'b0),
    .A_E_B(comparator_4_bit_1_a_e_b));  // open: A_G_B, A_L_B
  Comparator_4_bit comparator_4_bit_2 (
    .A(S), .B(4'b0010), .A_greater_B(1'b0), .A_equals_B(1'b1), .A_lesser_B(1'b0),
    .A_E_B(comparator_4_bit_2_a_e_b));  // open: A_G_B, A_L_B
  or or_1 (or_1_out, comparator_4_bit_1_a_e_b, comparator_4_bit_2_a_e_b);
  // Probe on Decision
  and and_1 (HALT, or_1_out, Flag);
  Multiplexer_4_to_1_16bits multiplexer_4_to_1_16bits_5 (
    .I_0(multiplexer_4_to_1_16bits_1_decision), .I_1(multiplexer_4_to_1_16bits_2_decision),
    .I_2(multiplexer_4_to_1_16bits_3_decision), .I_3(multiplexer_4_to_1_16bits_4_decision), .S_0(S[2]),
    .S_1(S[3]), .Decision(Decision));
  assign Carry_overflow = {{15{1'b0}}, multiplier_16_bits_1_carry_out[0]} | {{15{1'b0}}, fulladder_16_bit_1_carry_out[0]};  // OR_Gate or_2, 16 bits wide
  assign Dout = OE ? Decision : 16'bz;  // Controlled_Buffer controlled_buffer_1
endmodule

module Comparator_Encoder (
  input  A_greater_B,
  input  A_equals_B,
  input  A_lesser_B,
  output [15:0] Encoded
);

  wire [15:0] and_1_out, and_2_out, and_3_out, bit_extender_1_out, bit_extender_2_out, bit_extender_3_out;

  assign bit_extender_1_out = {{15{A_greater_B}}, A_greater_B};  // Bit_Extender bit_extender_1
  assign bit_extender_2_out = {{15{A_equals_B}}, A_equals_B};  // Bit_Extender bit_extender_2
  assign bit_extender_3_out = {{15{A_lesser_B}}, A_lesser_B};  // Bit_Extender bit_extender_3
  assign and_1_out = bit_extender_1_out & 16'h4;  // AND_Gate and_1, 16 bits wide
  assign and_2_out = bit_extender_2_out & 16'h2;  // AND_Gate and_2, 16 bits wide
  assign and_3_out = bit_extender_3_out & 16'h1;  // AND_Gate and_3, 16 bits wide
  assign Encoded = and_1_out | and_2_out | and_3_out;  // OR_Gate or_1, 16 bits wide
endmodule

module OpCode_Decoder (
  input  I_4,
  input  I_3,
  input  I_2,
  input  I_1,
  input  I_0,
  output O1,
  output O2,
  output O3,
  output O4,
  output O5,
  output O6,
  output O7,
  output O8,
  output O9,
  output O10,
  output O11,
  output O12,
  output O13,
  output O14,
  output O15,
  output O16,
  output O17,
  output O18,
  output O19,
  output O20,
  output O21,
  output O22,
  output O23,
  output O24,
  output O25,
  output O26,
  output O27,
  output O28,
  output O29,
  output O30,
  output O31,
  output O32
);

  wire not_1_out, not_2_out, not_3_out, not_4_out, not_5_out;

  not not_1 (not_1_out, I_4);
  not not_2 (not_2_out, I_3);
  not not_3 (not_3_out, I_2);
  not not_4 (not_4_out, I_1);
  not not_5 (not_5_out, I_0);
  and and_1 (O1, not_1_out, not_2_out, not_3_out, not_4_out, not_5_out);
  and and_2 (O2, not_1_out, not_2_out, not_3_out, not_4_out, I_0);
  and and_3 (O3, not_1_out, not_2_out, not_3_out, I_1, not_5_out);
  and and_4 (O4, not_1_out, not_2_out, not_3_out, I_1, I_0);
  and and_5 (O5, not_1_out, not_2_out, I_2, not_4_out, not_5_out);
  and and_6 (O6, not_1_out, not_2_out, I_2, not_4_out, I_0);
  and and_7 (O7, not_1_out, not_2_out, I_2, I_1, not_5_out);
  and and_8 (O8, not_1_out, not_2_out, I_2, I_1, I_0);
  and and_9 (O9, not_1_out, I_3, not_3_out, not_4_out, not_5_out);
  and and_10 (O10, not_1_out, I_3, not_3_out, not_4_out, I_0);
  and and_11 (O11, not_1_out, I_3, not_3_out, I_1, not_5_out);
  and and_12 (O12, not_1_out, I_3, not_3_out, I_1, I_0);
  and and_13 (O13, not_1_out, I_3, I_2, not_4_out, not_5_out);
  and and_14 (O14, not_1_out, I_3, I_2, not_4_out, I_0);
  and and_15 (O15, not_1_out, I_3, I_2, I_1, not_5_out);
  and and_16 (O16, not_1_out, I_3, I_2, I_1, I_0);
  and and_17 (O17, I_4, not_2_out, not_3_out, not_4_out, not_5_out);
  and and_18 (O18, I_4, not_2_out, not_3_out, not_4_out, I_0);
  and and_19 (O19, I_4, not_2_out, not_3_out, I_1, not_5_out);
  and and_20 (O20, I_4, not_2_out, not_3_out, I_1, I_0);
  and and_21 (O21, I_4, not_2_out, I_2, not_4_out, not_5_out);
  and and_22 (O22, I_4, not_2_out, I_2, not_4_out, I_0);
  and and_23 (O23, I_4, not_2_out, I_2, I_1, not_5_out);
  and and_24 (O24, I_4, not_2_out, I_2, I_1, I_0);
  and and_25 (O25, I_4, I_3, not_3_out, not_4_out, not_5_out);
  and and_26 (O26, I_4, I_3, not_3_out, not_4_out, I_0);
  and and_27 (O27, I_4, I_3, not_3_out, I_1, not_5_out);
  and and_28 (O28, I_4, I_3, not_3_out, I_1, I_0);
  and and_29 (O29, I_4, I_3, I_2, not_4_out, not_5_out);
  and and_30 (O30, I_4, I_3, I_2, not_4_out, I_0);
  and and_31 (O31, I_4, I_3, I_2, I_1, not_5_out);
  and and_32 (O32, I_4, I_3, I_2, I_1, I_0);
endmodule

module notMain (
  input  Counter_Reset,
  input  Sys_RAM_OE,
  input  Sys_RAM_WE,
  input  Inst_RAM_OE,
  input  Inst_RAM_WE,
  input  RAM_A_OE,
  input  RAM_A_WE,
  input  RAM_B_OE,
  input  RAM_B_WE,
  input  WE_MAR_Zero,
  input  WE_MAR_A,
  input  WE_MAR_B,
  input  WE_MBR_Zero,
  input  WE_MBR_A,
  input  WE_MBR_B,
  input  MBR_Zero_CB,
  input  MBR_A_CB,
  input  MBR_B_CB,
  input  Reg_1_WE,
  input  Reg_2_WE,
  input  Reg_3_WE,
  input  Reg_4_WE,
  input  Reg_5_WE,
  input  Reg_6_WE,
  input  Reg_7_WE,
  input  Reg_8_WE,
  input  WE_IR,
  input  OE_ALU,
  input  Out_WE,
  input  Reg_1_CB,
  input  Reg_5_CB,
  input  Reg_Out_CB,
  input  OpCode_WE,
  input  Three_Increm_Out,
  input  Two_Increm_Out,
  input  Count_enable,
  input  Counter_Increment_By_1,
  input  MAR_Z_term_CB1,
  input  MAR_Z_term_CB2,
  input  Terminal_WE,
  input  Counter_CB,
  input  Move_A_to_B,
  input  Terminal_Out,
  input  C_Term,
  input  B_Term,
  input  A_TERM,
  input  R_Swap_WE,
  input  Reg_Out_Carry_WE,
  input  Reg_2_CB,
  input  Reg_3_CB,
  input  Reg_4_CB,
  input  Reg_6_CB,
  input  Reg_7_CB,
  input  Reg_8_CB,
  input  MAR_Increm_In,
  input  One_Increm_Out,
  input  MATMULT_WE,
  input  OpCode_init_CB,
  input  ROM_Reset,
  input  MATMULT_00,
  input  MATMULT_10,
  input  MATMULT_01,
  input  MATMULT_11,
  input  Debug_WE,
  input  Destination2,
  output [4:0] MAR_A_Content,
  output [4:0] Content_of_counter,
  output [4:0] MAR_B_Content,
  output [15:0] IR_Content,
  output [15:0] ALU_Result
);

  wire alu_1_halt, and_1_out, clock_CPU_out, custom_clock_1_clock_out, Instruction_Register_flag, not_1_out,
       not_2_out, not_3_out, not_4_out, not_5_out, not_6_out, not_7_out, not_8_out, not_9_out, or_1_out,
       or_2_out, or_3_out, terminal_1_a_out, terminal_1_b_out;
  wire [0:0] not_10_out;
  wire [1:0] Instruction_Register_address_b;
  wire [2:0] Instruction_Register_address_b_2;
  wire [3:0] controlled_buffer_1_out;
  wire [4:0] address_switch_1_to_mar_z_from_a, controlled_buffer_3_out, controlled_buffer_10_out,
       controlled_buffer_25_out, controlled_buffer_32_out, controlled_buffer_39_out,
       controlled_buffer_54_out, controlled_buffer_56_out, Incrementer_new_mar_a1, Incrementer_new_mar_a2,
       Incrementer_new_mar_a3, Incrementer_new_mar_b1, Incrementer_new_mar_b2, Incrementer_new_mar_b3,
       Incrementer_new_mar_z1, Incrementer_new_mar_z2, Incrementer_new_mar_z3,
       Instruction_Register_address_a, Instruction_Register_op_code, MAR_A_dout, MAR_B_dout, MAR_Zero_q,
       undriven;
  wire [4:4] controlled_buffer_1_out_2, register_1_q;
  wire [7:0] Reg_1_q, Reg_1_q_2, Reg_2_q, Reg_2_q_2, Reg_3_q, Reg_3_q_2, Reg_4_q, Reg_4_q_2, Reg_5_q,
       Reg_5_q_2, Reg_6_q, Reg_6_q_2, Reg_7_q, Reg_7_q_2, Reg_8_q, Reg_8_q_2, register_1_q_2;
  wire [15:0] alu_1_carry_overflow, alu_1_dout, controlled_buffer_4_out, controlled_buffer_7_out,
       controlled_buffer_11_out, controlled_buffer_12_out, controlled_buffer_14_out,
       controlled_buffer_15_out, controlled_buffer_26_out, controlled_buffer_30_out,
       controlled_buffer_55_out, Data_A_dout, Data_B_dout, INST_dout, matmult_1_result_00,
       matmult_1_result_01, matmult_1_result_10, matmult_1_result_11, MBR_A_q, MBR_B_q, MBR_Zero_q,
       Reg_Out_carry_q, Reg_Out_q, register_swap_1_register_1_out, register_swap_1_register_2_out,
       register_swap_1_register_3_out, register_swap_1_register_4_out, register_swap_1_register_5_out,
       register_swap_1_register_6_out, register_swap_1_register_7_out, register_swap_1_register_8_out,
       System_dout, terminal_1_to_mbr_a, terminal_1_to_mbr_b, terminal_1_to_mbr_z;
  wire [31:0] ROM_1_CU_data, ROM_2_CU_data;

  Custom_clock custom_clock_1 (
    .Clock_In(clock_CPU_out), .HALT_Debug(alu_1_halt), .Debug_Val(Instruction_Register_address_a),
    .Debug_WE(ROM_2_CU_data[1]), .Clock_Out(custom_clock_1_clock_out));
  Clock clock_CPU (.out(clock_CPU_out));
  Counter #(.max('h10), .ongoal("continue"), .width(5)) Program_Counter (
    .clr(Counter_Reset), .up(ROM_2_CU_data[29]), .count(ROM_2_CU_data[28]), .clk(custom_clock_1_clock_out),
    .D(undriven), .Q(Content_of_counter));  // open: load, carry
  Register #(.width(5)) register_1 (
    .D({controlled_buffer_1_out_2[4], controlled_buffer_1_out}), .en(ROM_1_CU_data[0]),
    .clk(custom_clock_1_clock_out), .Q({register_1_q[4], register_1_q_2[7:4]}));  // open: clr
  assign {controlled_buffer_1_out_2[4], controlled_buffer_1_out} = not_1_out ? Instruction_Register_op_code : 5'bz;  // Controlled_Buffer controlled_buffer_1
  not not_1 (not_1_out, ROM_2_CU_data[7]);
  assign {controlled_buffer_1_out_2[4], controlled_buffer_1_out} = ROM_2_CU_data[7] ? {5{1'b0}} : 5'bz;  // Controlled_Buffer controlled_buffer_2
  // Probe on ALU_Result
  // Probe on Content_of_counter
  ALU alu_1 (
    .A(controlled_buffer_14_out), .B(controlled_buffer_15_out), .Flag(Instruction_Register_flag),
    .S(controlled_buffer_1_out), .OE(ROM_1_CU_data[5]), .Carry_overflow(alu_1_carry_overflow),
    .Dout(alu_1_dout), .Decision(ALU_Result), .HALT(alu_1_halt));
  MatMult matmult_1 (
    .A_00(Reg_1_q), .A_01(Reg_2_q), .A_10(Reg_3_q), .A_11(Reg_4_q), .B_00(Reg_5_q), .B_01(Reg_6_q),
    .B_10(Reg_7_q), .B_11(Reg_8_q), .WE(ROM_2_CU_data[8]), .Clock(custom_clock_1_clock_out),
    .Flag(Instruction_Register_flag), .Result_00(matmult_1_result_00), .Result_10(matmult_1_result_10),
    .Result_01(matmult_1_result_01), .Result_11(matmult_1_result_11));
  assign controlled_buffer_3_out = ROM_2_CU_data[24] ? Content_of_counter : 5'bz;  // Controlled_Buffer controlled_buffer_3
  Register #(.width(16)) Reg_Out (
    .D(alu_1_dout), .en(ROM_1_CU_data[4]), .clk(custom_clock_1_clock_out), .Q(Reg_Out_q));  // open: clr
  Register #(.width(16)) Reg_Out_carry (
    .D(alu_1_carry_overflow), .en(ROM_2_CU_data[17]), .clk(custom_clock_1_clock_out), .Q(Reg_Out_carry_q));  // open: clr
  assign controlled_buffer_4_out = ROM_2_CU_data[5] ? matmult_1_result_00 : 16'bz;  // Controlled_Buffer controlled_buffer_4
  assign controlled_buffer_4_out = ROM_2_CU_data[4] ? matmult_1_result_10 : 16'bz;  // Controlled_Buffer controlled_buffer_5
  assign controlled_buffer_4_out = ROM_2_CU_data[3] ? matmult_1_result_01 : 16'bz;  // Controlled_Buffer controlled_buffer_6
  assign controlled_buffer_7_out = not_2_out ? Reg_Out_q : 16'bz;  // Controlled_Buffer controlled_buffer_7
  not not_2 (not_2_out, Instruction_Register_flag);
  assign controlled_buffer_7_out = Instruction_Register_flag ? Reg_Out_carry_q : 16'bz;  // Controlled_Buffer controlled_buffer_8
  assign controlled_buffer_4_out = ROM_2_CU_data[2] ? matmult_1_result_11 : 16'bz;  // Controlled_Buffer controlled_buffer_9
  or or_1 (or_1_out, ROM_2_CU_data[2], ROM_2_CU_data[3], ROM_2_CU_data[5], ROM_2_CU_data[4]);
  assign controlled_buffer_10_out = not_4_out ? {Instruction_Register_address_b_2, Instruction_Register_address_b} : 5'bz;  // Controlled_Buffer controlled_buffer_10
  Instruction_Splitter Instruction_Register (
    .Instruction(IR_Content), .WE(ROM_1_CU_data[6]), .Clock(custom_clock_1_clock_out),
    .Address_B({Instruction_Register_address_b_2, Instruction_Register_address_b}),
    .Address_A(Instruction_Register_address_a), .OP_Code(Instruction_Register_op_code),
    .Flag(Instruction_Register_flag));
  assign controlled_buffer_11_out = not_3_out ? controlled_buffer_7_out : 16'bz;  // Controlled_Buffer controlled_buffer_11
  assign controlled_buffer_12_out = ROM_1_CU_data[1] ? controlled_buffer_11_out : 16'bz;  // Controlled_Buffer controlled_buffer_12
  not not_3 (not_3_out, or_1_out);
  assign controlled_buffer_11_out = or_1_out ? controlled_buffer_4_out : 16'bz;  // Controlled_Buffer controlled_buffer_13
  not not_4 (not_4_out, and_1_out);
  // Probe on controlled_buffer_10_out
  // Probe on Instruction_Register_address_a
  Register #(.width(16)) Reg_1 (
    .D(controlled_buffer_14_out), .en(ROM_1_CU_data[14]), .clk(custom_clock_1_clock_out),
    .Q({Reg_1_q_2, Reg_1_q}));  // open: clr
  Register #(.width(16)) Reg_3 (
    .D(controlled_buffer_14_out), .en(ROM_1_CU_data[12]), .clk(custom_clock_1_clock_out),
    .Q({Reg_3_q_2, Reg_3_q}));  // open: clr
  and and_1 (and_1_out, Instruction_Register_flag, ROM_2_CU_data[23]);
  assign controlled_buffer_14_out = ROM_1_CU_data[3] ? {Reg_1_q_2, Reg_1_q} : 16'bz;  // Controlled_Buffer controlled_buffer_14
  Register #(.width(16)) Reg_5 (
    .D(controlled_buffer_15_out), .en(ROM_1_CU_data[10]), .clk(custom_clock_1_clock_out),
    .Q({Reg_5_q_2, Reg_5_q}));  // open: clr
  Register #(.width(16)) Reg_7 (
    .D(controlled_buffer_15_out), .en(ROM_1_CU_data[8]), .clk(custom_clock_1_clock_out),
    .Q({Reg_7_q_2, Reg_7_q}));  // open: clr
  Address_Switch address_switch_1 (
    .Address_A(Instruction_Register_address_a), .Destination_B(Instruction_Register_address_b),
    .To_MAR_Z_from_A(address_switch_1_to_mar_z_from_a));
  Register #(.width(16)) Reg_2 (
    .D(controlled_buffer_14_out), .en(ROM_1_CU_data[13]), .clk(custom_clock_1_clock_out),
    .Q({Reg_2_q_2, Reg_2_q}));  // open: clr
  Register #(.width(16)) Reg_4 (
    .D(controlled_buffer_14_out), .en(ROM_1_CU_data[11]), .clk(custom_clock_1_clock_out),
    .Q({Reg_4_q_2, Reg_4_q}));  // open: clr
  assign controlled_buffer_15_out = ROM_1_CU_data[2] ? {Reg_5_q_2, Reg_5_q} : 16'bz;  // Controlled_Buffer controlled_buffer_15
  assign controlled_buffer_3_out = ROM_2_CU_data[26] ? {Instruction_Register_address_b_2, Instruction_Register_address_b} : 5'bz;  // Controlled_Buffer controlled_buffer_16
  assign controlled_buffer_3_out = ROM_2_CU_data[27] ? address_switch_1_to_mar_z_from_a : 5'bz;  // Controlled_Buffer controlled_buffer_17
  Register #(.width(16)) Reg_6 (
    .D(controlled_buffer_15_out), .en(ROM_1_CU_data[9]), .clk(custom_clock_1_clock_out),
    .Q({Reg_6_q_2, Reg_6_q}));  // open: clr
  Register #(.width(16)) Reg_8 (
    .D(controlled_buffer_15_out), .en(ROM_1_CU_data[7]), .clk(custom_clock_1_clock_out),
    .Q({Reg_8_q_2, Reg_8_q}));  // open: clr
  assign controlled_buffer_14_out = ROM_2_CU_data[15] ? {Reg_3_q_2, Reg_3_q} : 16'bz;  // Controlled_Buffer controlled_buffer_18
  assign controlled_buffer_10_out = and_1_out ? Instruction_Register_address_a : 5'bz;  // Controlled_Buffer controlled_buffer_19
  assign controlled_buffer_14_out = ROM_2_CU_data[16] ? {Reg_2_q_2, Reg_2_q} : 16'bz;  // Controlled_Buffer controlled_buffer_20
  assign controlled_buffer_14_out = ROM_2_CU_data[14] ? {Reg_4_q_2, Reg_4_q} : 16'bz;  // Controlled_Buffer controlled_buffer_21
  assign controlled_buffer_15_out = ROM_2_CU_data[13] ? {Reg_6_q_2, Reg_6_q} : 16'bz;  // Controlled_Buffer controlled_buffer_22
  assign controlled_buffer_15_out = ROM_2_CU_data[12] ? {Reg_7_q_2, Reg_7_q} : 16'bz;  // Controlled_Buffer controlled_buffer_23
  assign controlled_buffer_15_out = ROM_2_CU_data[11] ? {Reg_8_q_2, Reg_8_q} : 16'bz;  // Controlled_Buffer controlled_buffer_24
  // Probe on controlled_buffer_14_out
  Register #(.width(5)) MAR_Zero (
    .D(controlled_buffer_3_out), .en(ROM_1_CU_data[23]), .clk(custom_clock_1_clock_out), .Q(MAR_Zero_q));  // open: clr
  MAR MAR_A (
    .Clock(custom_clock_1_clock_out), .WE(ROM_1_CU_data[22]), .Din(Instruction_Register_address_a),
    .OE(1'b1), .Dout(MAR_A_dout), .Stored_Data(MAR_A_Content));
  MAR MAR_B (
    .Clock(custom_clock_1_clock_out), .WE(ROM_1_CU_data[21]), .Din(controlled_buffer_10_out), .OE(1'b1),
    .Dout(MAR_B_dout), .Stored_Data(MAR_B_Content));
  or or_2 (or_2_out, or_3_out, ROM_1_CU_data[1]);
  assign controlled_buffer_25_out = ROM_2_CU_data[10] ? MAR_Zero_q : 5'bz;  // Controlled_Buffer controlled_buffer_25
  not not_5 (not_5_out, or_2_out);
  // Probe on Data_B_dout
  or or_3 (or_3_out, ROM_2_CU_data[5], ROM_2_CU_data[4], ROM_2_CU_data[3], ROM_2_CU_data[2]);
  assign controlled_buffer_26_out = ROM_2_CU_data[5] ? register_swap_1_register_1_out : 16'bz;  // Controlled_Buffer controlled_buffer_26
  Register_Swap register_swap_1 (
    .Address_A(Instruction_Register_address_a),
    .Address_B({Instruction_Register_address_b_2, Instruction_Register_address_b}),
    .Register_1_in({Reg_1_q_2, Reg_1_q}), .Register_2_in({Reg_2_q_2, Reg_2_q}),
    .Register_3_in({Reg_3_q_2, Reg_3_q}), .Register_4_in({Reg_4_q_2, Reg_4_q}),
    .Register_5_in({Reg_5_q_2, Reg_5_q}), .Register_6_in({Reg_6_q_2, Reg_6_q}),
    .Register_7_in({Reg_7_q_2, Reg_7_q}), .Register_8_in({Reg_8_q_2, Reg_8_q}),
    .R_Swap_WE(ROM_2_CU_data[18]), .Clock(custom_clock_1_clock_out),
    .Register_1_out(register_swap_1_register_1_out), .Register_2_out(register_swap_1_register_2_out),
    .Register_3_out(register_swap_1_register_3_out), .Register_4_out(register_swap_1_register_4_out),
    .Register_5_out(register_swap_1_register_5_out), .Register_6_out(register_swap_1_register_6_out),
    .Register_7_out(register_swap_1_register_7_out), .Register_8_out(register_swap_1_register_8_out));
  assign controlled_buffer_26_out = ROM_2_CU_data[4] ? register_swap_1_register_2_out : 16'bz;  // Controlled_Buffer controlled_buffer_27
  Terminal terminal_1 (
    .Clock(custom_clock_1_clock_out), .MBR_Z(IR_Content), .MBR_A(controlled_buffer_14_out),
    .MBR_B(controlled_buffer_15_out), .Terminal_WE(ROM_2_CU_data[25]),
    .Destination1(Instruction_Register_flag), .Destination2(ROM_2_CU_data[0]), .A_Term(ROM_2_CU_data[19]),
    .B_Term(ROM_2_CU_data[20]), .C_Term(ROM_2_CU_data[21]), .OPcode(Instruction_Register_op_code),
    .To_MBR_A(terminal_1_to_mbr_a), .To_MBR_B(terminal_1_to_mbr_b), .To_MBR_Z(terminal_1_to_mbr_z),
    .A_Out(terminal_1_a_out), .B_Out(terminal_1_b_out));
  assign controlled_buffer_26_out = ROM_2_CU_data[3] ? register_swap_1_register_3_out : 16'bz;  // Controlled_Buffer controlled_buffer_28
  assign controlled_buffer_26_out = ROM_2_CU_data[2] ? register_swap_1_register_4_out : 16'bz;  // Controlled_Buffer controlled_buffer_29
  assign controlled_buffer_30_out = ROM_2_CU_data[5] ? register_swap_1_register_5_out : 16'bz;  // Controlled_Buffer controlled_buffer_30
  assign controlled_buffer_30_out = ROM_2_CU_data[4] ? register_swap_1_register_6_out : 16'bz;  // Controlled_Buffer controlled_buffer_31
  assign controlled_buffer_32_out = ROM_2_CU_data[10] ? MAR_A_dout : 5'bz;  // Controlled_Buffer controlled_buffer_32
  // Probe on controlled_buffer_26_out
  assign controlled_buffer_26_out = not_5_out ? Data_A_dout : 16'bz;  // Controlled_Buffer controlled_buffer_33
  assign controlled_buffer_30_out = not_5_out ? Data_B_dout : 16'bz;  // Controlled_Buffer controlled_buffer_34
  assign controlled_buffer_26_out = ROM_2_CU_data[22] ? terminal_1_to_mbr_a : 16'bz;  // Controlled_Buffer controlled_buffer_35
  assign controlled_buffer_30_out = ROM_2_CU_data[22] ? terminal_1_to_mbr_b : 16'bz;  // Controlled_Buffer controlled_buffer_36
  // Probe on terminal_1_to_mbr_b
  assign controlled_buffer_30_out = ROM_2_CU_data[3] ? register_swap_1_register_7_out : 16'bz;  // Controlled_Buffer controlled_buffer_37
  assign controlled_buffer_30_out = ROM_2_CU_data[2] ? register_swap_1_register_8_out : 16'bz;  // Controlled_Buffer controlled_buffer_38
  assign controlled_buffer_39_out = ROM_2_CU_data[10] ? MAR_B_dout : 5'bz;  // Controlled_Buffer controlled_buffer_39
  Register #(.width(16)) MBR_A (
    .D(controlled_buffer_26_out), .en(ROM_1_CU_data[19]), .clk(custom_clock_1_clock_out), .Q(MBR_A_q));  // open: clr
  Register #(.width(16)) MBR_B (
    .D(controlled_buffer_30_out), .en(ROM_1_CU_data[18]), .clk(custom_clock_1_clock_out), .Q(MBR_B_q));  // open: clr
  assign controlled_buffer_12_out = ROM_2_CU_data[22] ? terminal_1_to_mbr_z : 16'bz;  // Controlled_Buffer controlled_buffer_40
  Register #(.width(16)) MBR_Zero (
    .D(controlled_buffer_12_out), .en(ROM_1_CU_data[20]), .clk(custom_clock_1_clock_out), .Q(MBR_Zero_q));  // open: clr
  MARS_Increm Incrementer (
    .MAR_Z(controlled_buffer_25_out), .MAR_A(controlled_buffer_32_out), .MAR_B(controlled_buffer_39_out),
    .WE(ROM_2_CU_data[10]), .Clock(custom_clock_1_clock_out), .New_MAR_Z3(Incrementer_new_mar_z3),
    .New_MAR_Z2(Incrementer_new_mar_z2), .New_MAR_Z1(Incrementer_new_mar_z1),
    .New_MAR_A3(Incrementer_new_mar_a3), .New_MAR_A2(Incrementer_new_mar_a2),
    .New_MAR_A1(Incrementer_new_mar_a1), .New_MAR_B3(Incrementer_new_mar_b3),
    .New_MAR_B2(Incrementer_new_mar_b2), .New_MAR_B1(Incrementer_new_mar_b1));
  assign controlled_buffer_25_out = ROM_2_CU_data[9] ? Incrementer_new_mar_z1 : 5'bz;  // Controlled_Buffer controlled_buffer_41
  assign controlled_buffer_25_out = ROM_2_CU_data[30] ? Incrementer_new_mar_z2 : 5'bz;  // Controlled_Buffer controlled_buffer_42
  assign controlled_buffer_25_out = ROM_2_CU_data[31] ? Incrementer_new_mar_z3 : 5'bz;  // Controlled_Buffer controlled_buffer_43
  assign IR_Content = ROM_1_CU_data[17] ? MBR_Zero_q : 16'bz;  // Controlled_Buffer controlled_buffer_44
  assign controlled_buffer_32_out = ROM_2_CU_data[9] ? Incrementer_new_mar_a1 : 5'bz;  // Controlled_Buffer controlled_buffer_45
  assign controlled_buffer_32_out = ROM_2_CU_data[30] ? Incrementer_new_mar_a2 : 5'bz;  // Controlled_Buffer controlled_buffer_46
  assign controlled_buffer_32_out = ROM_2_CU_data[31] ? Incrementer_new_mar_a3 : 5'bz;  // Controlled_Buffer controlled_buffer_47
  assign controlled_buffer_14_out = ROM_1_CU_data[16] ? MBR_A_q : 16'bz;  // Controlled_Buffer controlled_buffer_48
  assign controlled_buffer_15_out = ROM_1_CU_data[15] ? MBR_B_q : 16'bz;  // Controlled_Buffer controlled_buffer_49
  assign controlled_buffer_39_out = ROM_2_CU_data[9] ? Incrementer_new_mar_b1 : 5'bz;  // Controlled_Buffer controlled_buffer_50
  assign controlled_buffer_39_out = ROM_2_CU_data[30] ? Incrementer_new_mar_b2 : 5'bz;  // Controlled_Buffer controlled_buffer_51
  assign controlled_buffer_12_out = not_6_out ? controlled_buffer_55_out : 16'bz;  // Controlled_Buffer controlled_buffer_52
  assign controlled_buffer_39_out = ROM_2_CU_data[31] ? Incrementer_new_mar_b3 : 5'bz;  // Controlled_Buffer controlled_buffer_53
  not not_6 (not_6_out, ROM_1_CU_data[1]);
  // Probe on controlled_buffer_54_out
  assign controlled_buffer_54_out = not_7_out ? controlled_buffer_32_out : 5'bz;  // Controlled_Buffer controlled_buffer_54
  not not_7 (not_7_out, terminal_1_b_out);
  RAM #(.addrWidth(5), .dataWidth(16)) Data_A (
    .addr(controlled_buffer_54_out), .we(ROM_1_CU_data[26]), .oe(ROM_1_CU_data[27]),
    .clk(custom_clock_1_clock_out), .din(controlled_buffer_14_out), .dout(Data_A_dout));
  RAM #(.addrWidth(5), .dataWidth(16)) INST (
    .addr(controlled_buffer_25_out), .we(ROM_1_CU_data[28]), .oe(ROM_1_CU_data[29]),
    .clk(custom_clock_1_clock_out), .din(IR_Content), .dout(INST_dout));
  // Probe on controlled_buffer_56_out
  not not_8 (not_8_out, ROM_1_CU_data[31]);
  assign controlled_buffer_55_out = not_8_out ? INST_dout : 16'bz;  // Controlled_Buffer controlled_buffer_55
  assign controlled_buffer_56_out = not_9_out ? controlled_buffer_39_out : 5'bz;  // Controlled_Buffer controlled_buffer_56
  not not_9 (not_9_out, terminal_1_a_out);
  RAM #(.addrWidth(5), .dataWidth(16)) System (
    .addr(controlled_buffer_25_out), .we(ROM_1_CU_data[30]), .oe(ROM_1_CU_data[31]),
    .clk(custom_clock_1_clock_out), .din(IR_Content), .dout(System_dout));
  assign controlled_buffer_55_out = ROM_1_CU_data[31] ? System_dout : 16'bz;  // Controlled_Buffer controlled_buffer_57
  RAM #(.addrWidth(5), .dataWidth(16)) Data_B (
    .addr(controlled_buffer_56_out), .we(ROM_1_CU_data[24]), .oe(ROM_1_CU_data[25]),
    .clk(custom_clock_1_clock_out), .din(controlled_buffer_15_out), .dout(Data_B_dout));
  ROM #(.dataWidth(32)) ROM_1_CU (.addr(register_1_q_2), .data(ROM_1_CU_data));
  ROM #(.dataWidth(32)) ROM_2_CU (.addr(register_1_q_2), .data(ROM_2_CU_data));
  not not_10 (not_10_out[0], ROM_2_CU_data[6]);
  Counter #(.max('hf), .ongoal("continue"), .width(4)) ROM_Counter (
    .load(ROM_2_CU_data[6]), .up(1'b1), .count(1'b1), .clk(custom_clock_1_clock_out),
    .D({3'b000, not_10_out[0]}), .Q(register_1_q_2[3:0]));  // open: clr, carry

  // Notes on the sheet:
  //   Initial OpCode
  //   Current OpCode
  //   MBR A Registers
  //   MBR B Resgisters
  //   Current OpCode
  //   contents of ROM_1_CU (hex, n*v repeats v):
  //   800000 20100000 100000 20040 1 11*0 600000 a6c0000 dc400 1c400 3d 1 11*0 1 14*0 600000 a6c0000 dc400
  //   1c400 3d 1 10*0 800000 100002 40020000 1 12*0 600000 a6c0000 c0000 18000 40002 80002 5018000 1 9*0
  //   c0000 1c400 c0000 1a200 c0000 19100 c0000 18880 1 6*0 600000 a6c0000 dc400 1c400 a0c0000 da200 1a200
  //   a0c0000 d9100 19100 a0c0000 d8880 18880 1 0 0 800000 100002 40020000 100002 40020000 100002 40020000
  //   100002 40020000 1 6*0 600000 1 14*0 600000 a6c0000 dc400 1c400 3d 1 10*0 600000 a6c0000 dc400 1c400
  //   3d 1 10*0 600000 a6c0000 dc400 1c400 3d 1 10*0 600000 a6c0000 dc400 1c400 3d 1 10*0 1 15*0 e00000
  //   80100000 80100000 20000 80002 40002 5018000 1
  //   All Signals
  //   contents of ROM_2_CU (hex, n*v repeats v):
  //   1000000 30000400 0 0 40 12*0 400 0 0 20000 c0 10*0 2 c0 15*0 400 0 0 20000 c0 10*0 8000000 0 400 c0
  //   13*0 400 0 2000000 500000 600001 400 c0 8*0 40000 20 0 10 0 8 0 4 0 c0 7*0 400 0 0 200 0 0 40000000
  //   0 0 80000000 0 0 c0 0 0 8000000 20 400 10 200 8 40000000 4 80000000 c0 6*0 100 c0 15*0 400 0 0 20000
  //   c0 11*0 400 0 0 20000 c0 11*0 400 0 0 20000 c0 11*0 400 0 0 20000 c0 10*0 c0 15*0 4800000 400 400
  //   2000000 480001 480001 401 c0
  //   Counter of ROM
endmodule

module Terminal (
  input  Clock,
  input  [15:0] MBR_Z,
  input  [15:0] MBR_A,
  input  [15:0] MBR_B,
  input  Terminal_WE,
  input  Destination1,
  input  Destination2,
  input  A_Term,
  input  B_Term,
  input  C_Term,
  input  [4:0] OPcode,
  output [15:0] To_MBR_A,
  output [15:0] To_MBR_B,
  output [15:0] To_MBR_Z,
  output A_Out,
  output B_Out
);

  wire and_1_out, and_2_out, and_3_out, and_4_out, comparator_4_bit_1_a_e_b, not_1_out, not_2_out, or_1_out;
  wire [15:0] controlled_buffer_1_out, Terminal_A_q, Terminal_B_q, Terminal_C_q;

  Register #(.width(16)) Terminal_A (.D(MBR_Z), .en(Terminal_WE), .clk(Clock), .Q(Terminal_A_q));  // open: clr
  Register #(.width(16)) Terminal_B (.D(MBR_A), .en(Terminal_WE), .clk(Clock), .Q(Terminal_B_q));  // open: clr
  Register #(.width(16)) Terminal_C (.D(MBR_B), .en(Terminal_WE), .clk(Clock), .Q(Terminal_C_q));  // open: clr
  not not_1 (not_1_out, Destination1);
  not not_2 (not_2_out, Destination2);
  assign controlled_buffer_1_out = A_Term ? Terminal_A_q : 16'bz;  // Controlled_Buffer controlled_buffer_1
  assign controlled_buffer_1_out = B_Term ? Terminal_B_q : 16'bz;  // Controlled_Buffer controlled_buffer_2
  assign controlled_buffer_1_out = C_Term ? Terminal_C_q : 16'bz;  // Controlled_Buffer controlled_buffer_3
  and and_1 (and_1_out, Destination1, not_2_out);
  and and_2 (and_2_out, not_1_out, Destination2);
  and and_3 (and_3_out, Destination1, Destination2);
  and and_4 (and_4_out, not_1_out, not_2_out);
  assign To_MBR_Z = and_1_out ? controlled_buffer_1_out : 16'bz;  // Controlled_Buffer controlled_buffer_4
  or or_1 (or_1_out, and_3_out, and_4_out);
  assign To_MBR_B = or_1_out ? controlled_buffer_1_out : 16'bz;  // Controlled_Buffer controlled_buffer_5
  assign To_MBR_A = and_2_out ? controlled_buffer_1_out : 16'bz;  // Controlled_Buffer controlled_buffer_6
  Comparator_4_bit comparator_4_bit_1 (
    .A(OPcode[3:0]), .B(4'b1111), .A_greater_B(1'b0), .A_equals_B(1'b1), .A_lesser_B(1'b0),
    .A_E_B(comparator_4_bit_1_a_e_b));  // open: A_G_B, A_L_B
  buf and_5 (A_Out, and_2_out);  // AND_Gate
  and and_6 (B_Out, or_1_out, comparator_4_bit_1_a_e_b);

  // Notes on the sheet:
  //   To MBR A
  //   To RAM A
  //   To RAM B
  //   To System RAM
  //   To MBR B
  //   To Instruction RAM
endmodule

module Address_Switch (
  input  [4:0] Address_A,
  input  [1:0] Destination_B,
  output [4:0] To_MAR_Z_from_A
);

  wire and_1_out, and_2_out, not_1_out, not_2_out, or_1_out;

  not not_1 (not_1_out, Destination_B[0]);
  not not_2 (not_2_out, Destination_B[1]);
  and and_1 (and_1_out, not_1_out, not_2_out);
  and and_2 (and_2_out, Destination_B[0], not_2_out);
  or or_1 (or_1_out, and_1_out, and_2_out);
  assign To_MAR_Z_from_A = or_1_out ? Address_A : 5'bz;  // Controlled_Buffer controlled_buffer_1
endmodule

module MatMult (
  input  [7:0] A_00,
  input  [7:0] A_01,
  input  [7:0] A_10,
  input  [7:0] A_11,
  input  [7:0] B_00,
  input  [7:0] B_01,
  input  [7:0] B_10,
  input  [7:0] B_11,
  input  WE,
  input  Clock,
  input  Flag,
  output [15:0] Result_00,
  output [15:0] Result_10,
  output [15:0] Result_01,
  output [15:0] Result_11
);

  wire not_1_out;
  wire [0:0] fulladder_16_bit_1_carry_out, fulladder_16_bit_2_carry_out, fulladder_16_bit_3_carry_out,
       fulladder_16_bit_4_carry_out;
  wire [15:0] controlled_buffer_1_out, controlled_buffer_2_out, controlled_buffer_3_out,
       controlled_buffer_4_out, fulladder_16_bit_1_sums, fulladder_16_bit_2_sums, fulladder_16_bit_3_sums,
       fulladder_16_bit_4_sums, multiplier_16_bits_1_product, multiplier_16_bits_2_product,
       multiplier_16_bits_3_product, multiplier_16_bits_4_product, multiplier_16_bits_5_product,
       multiplier_16_bits_6_product, multiplier_16_bits_7_product, multiplier_16_bits_8_product;

  // Probe on A_00
  // Probe on B_00
  // Probe on A_01
  // Probe on A_10
  // Probe on A_11
  // Probe on B_01
  // Probe on B_10
  // Probe on B_11
  Multiplier_16_bits multiplier_16_bits_1 (
    .A(A_00), .B(B_00), .Product(multiplier_16_bits_1_product));  // open: Carry_Out
  Multiplier_16_bits multiplier_16_bits_2 (
    .A(A_01), .B(B_10), .Product(multiplier_16_bits_2_product));  // open: Carry_Out
  Multiplier_16_bits multiplier_16_bits_3 (
    .A(A_10), .B(B_00), .Product(multiplier_16_bits_3_product));  // open: Carry_Out
  Multiplier_16_bits multiplier_16_bits_4 (
    .A(A_11), .B(B_10), .Product(multiplier_16_bits_4_product));  // open: Carry_Out
  Multiplier_16_bits multiplier_16_bits_5 (
    .A(A_00), .B(B_01), .Product(multiplier_16_bits_5_product));  // open: Carry_Out
  Multiplier_16_bits multiplier_16_bits_6 (
    .A(A_01), .B(B_11), .Product(multiplier_16_bits_6_product));  // open: Carry_Out
  Multiplier_16_bits multiplier_16_bits_7 (
    .A(A_10), .B(B_01), .Product(multiplier_16_bits_7_product));  // open: Carry_Out
  Multiplier_16_bits multiplier_16_bits_8 (
    .A(A_11), .B(B_11), .Product(multiplier_16_bits_8_product));  // open: Carry_Out
  not not_1 (not_1_out, Flag);
  // Probe on fulladder_16_bit_1_sums
  FullAdder_16_bit fulladder_16_bit_1 (
    .A(multiplier_16_bits_1_product), .B(multiplier_16_bits_2_product),
    .Carry_out(fulladder_16_bit_1_carry_out[0]), .Sums(fulladder_16_bit_1_sums));  // open: Carry_in, Sub, Negative
  // Probe on fulladder_16_bit_2_sums
  FullAdder_16_bit fulladder_16_bit_2 (
    .A(multiplier_16_bits_3_product), .B(multiplier_16_bits_4_product),
    .Carry_out(fulladder_16_bit_2_carry_out[0]), .Sums(fulladder_16_bit_2_sums));  // open: Carry_in, Sub, Negative
  // Probe on fulladder_16_bit_3_sums
  FullAdder_16_bit fulladder_16_bit_3 (
    .A(multiplier_16_bits_5_product), .B(multiplier_16_bits_6_product),
    .Carry_out(fulladder_16_bit_3_carry_out[0]), .Sums(fulladder_16_bit_3_sums));  // open: Carry_in, Sub, Negative
  // Probe on fulladder_16_bit_4_sums
  FullAdder_16_bit fulladder_16_bit_4 (
    .A(multiplier_16_bits_7_product), .B(multiplier_16_bits_8_product),
    .Carry_out(fulladder_16_bit_4_carry_out[0]), .Sums(fulladder_16_bit_4_sums));  // open: Carry_in, Sub, Negative
  assign controlled_buffer_1_out = Flag ? {{15{1'b0}}, fulladder_16_bit_1_carry_out[0]} : 16'bz;  // Controlled_Buffer controlled_buffer_1
  assign controlled_buffer_2_out = Flag ? {{15{1'b0}}, fulladder_16_bit_2_carry_out[0]} : 16'bz;  // Controlled_Buffer controlled_buffer_2
  assign controlled_buffer_3_out = Flag ? {{15{1'b0}}, fulladder_16_bit_3_carry_out[0]} : 16'bz;  // Controlled_Buffer controlled_buffer_3
  assign controlled_buffer_4_out = Flag ? {{15{1'b0}}, fulladder_16_bit_4_carry_out[0]} : 16'bz;  // Controlled_Buffer controlled_buffer_4
  assign controlled_buffer_1_out = not_1_out ? fulladder_16_bit_1_sums : 16'bz;  // Controlled_Buffer controlled_buffer_5
  assign controlled_buffer_2_out = not_1_out ? fulladder_16_bit_2_sums : 16'bz;  // Controlled_Buffer controlled_buffer_6
  assign controlled_buffer_3_out = not_1_out ? fulladder_16_bit_3_sums : 16'bz;  // Controlled_Buffer controlled_buffer_7
  assign controlled_buffer_4_out = not_1_out ? fulladder_16_bit_4_sums : 16'bz;  // Controlled_Buffer controlled_buffer_8
  Register #(.width(16)) register_1 (.D(controlled_buffer_1_out), .en(WE), .clk(Clock), .Q(Result_00));  // open: clr
  Register #(.width(16)) register_2 (.D(controlled_buffer_2_out), .en(WE), .clk(Clock), .Q(Result_10));  // open: clr
  Register #(.width(16)) register_3 (.D(controlled_buffer_3_out), .en(WE), .clk(Clock), .Q(Result_01));  // open: clr
  Register #(.width(16)) register_4 (.D(controlled_buffer_4_out), .en(WE), .clk(Clock), .Q(Result_11));  // open: clr

  // Notes on the sheet:
  //   A
  //   B
  //   00
  //   01
  //   10
  //   11
  //   00
  //   01
  //   10
  //   11
endmodule

module MARS_Increm (
  input  [4:0] MAR_Z,
  input  [4:0] MAR_A,
  input  [4:0] MAR_B,
  input  WE,
  input  Clock,
  output [4:0] New_MAR_Z3,
  output [4:0] New_MAR_Z2,
  output [4:0] New_MAR_Z1,
  output [4:0] New_MAR_A3,
  output [4:0] New_MAR_A2,
  output [4:0] New_MAR_A1,
  output [4:0] New_MAR_B3,
  output [4:0] New_MAR_B2,
  output [4:0] New_MAR_B1
);

  wire [4:0] register_1_q, register_2_q, register_3_q;
  wire [15:5] fulladder_16_bit_1_sums, fulladder_16_bit_2_sums, fulladder_16_bit_3_sums,
       fulladder_16_bit_4_sums, fulladder_16_bit_5_sums, fulladder_16_bit_6_sums, fulladder_16_bit_7_sums,
       fulladder_16_bit_8_sums, fulladder_16_bit_9_sums;

  Register #(.width(5)) register_1 (.D(MAR_Z), .en(WE), .clk(Clock), .Q(register_1_q));  // open: clr
  Register #(.width(5)) register_2 (.D(MAR_A), .en(WE), .clk(Clock), .Q(register_2_q));  // open: clr
  Register #(.width(5)) register_3 (.D(MAR_B), .en(WE), .clk(Clock), .Q(register_3_q));  // open: clr
  FullAdder_16_bit fulladder_16_bit_1 (
    .A({{11{1'b0}}, register_1_q}), .B(16'h1), .Sums({fulladder_16_bit_1_sums, New_MAR_Z1}));  // open: Carry_in, Sub, Negative, Carry_out
  FullAdder_16_bit fulladder_16_bit_2 (
    .A({{11{1'b0}}, register_2_q}), .B(16'h1), .Sums({fulladder_16_bit_2_sums, New_MAR_A1}));  // open: Carry_in, Sub, Negative, Carry_out
  FullAdder_16_bit fulladder_16_bit_3 (
    .A({{11{1'b0}}, register_3_q}), .B(16'h1), .Sums({fulladder_16_bit_3_sums, New_MAR_B1}));  // open: Carry_in, Sub, Negative, Carry_out
  FullAdder_16_bit fulladder_16_bit_4 (
    .A(16'h1), .B({fulladder_16_bit_1_sums, New_MAR_Z1}), .Sums({fulladder_16_bit_4_sums, New_MAR_Z2}));  // open: Carry_in, Sub, Negative, Carry_out
  FullAdder_16_bit fulladder_16_bit_5 (
    .A(16'h1), .B({fulladder_16_bit_2_sums, New_MAR_A1}), .Sums({fulladder_16_bit_5_sums, New_MAR_A2}));  // open: Carry_in, Sub, Negative, Carry_out
  FullAdder_16_bit fulladder_16_bit_6 (
    .A(16'h1), .B({fulladder_16_bit_3_sums, New_MAR_B1}), .Sums({fulladder_16_bit_6_sums, New_MAR_B2}));  // open: Carry_in, Sub, Negative, Carry_out
  FullAdder_16_bit fulladder_16_bit_7 (
    .A(16'h1), .B({fulladder_16_bit_4_sums, New_MAR_Z2}), .Sums({fulladder_16_bit_7_sums, New_MAR_Z3}));  // open: Carry_in, Sub, Negative, Carry_out
  FullAdder_16_bit fulladder_16_bit_8 (
    .A(16'h1), .B({fulladder_16_bit_5_sums, New_MAR_A2}), .Sums({fulladder_16_bit_8_sums, New_MAR_A3}));  // open: Carry_in, Sub, Negative, Carry_out
  FullAdder_16_bit fulladder_16_bit_9 (
    .A(16'h1), .B({fulladder_16_bit_6_sums, New_MAR_B2}), .Sums({fulladder_16_bit_9_sums, New_MAR_B3}));  // open: Carry_in, Sub, Negative, Carry_out
endmodule

module Custom_clock (
  input  Clock_In,
  input  HALT_Debug,
  input  [4:0] Debug_Val,
  input  Debug_WE,
  output Clock_Out
);

  wire and_1_out, controlled_buffer_1_out, not_1_out, not_2_out, not_3_out, or_1_out;
  wire [4:0] controlled_buffer_2_out, counter_1_q, register_1_q;

  not not_1 (not_1_out, HALT_Debug);
  Register #(.width(5)) register_1 (.D(Debug_Val), .en(Debug_WE), .clk(Clock_In), .Q(register_1_q));  // open: clr
  and and_1 (and_1_out, Clock_In, not_1_out);
  assign controlled_buffer_1_out = not_3_out ? 1'b1 : 1'bz;  // Controlled_Buffer controlled_buffer_1
  assign controlled_buffer_2_out = not_2_out ? register_1_q : 5'bz;  // Controlled_Buffer controlled_buffer_2
  Counter #(.max('h1f), .width(5)) counter_1 (
    .load(controlled_buffer_1_out), .D(controlled_buffer_2_out), .count(1'b1), .Q(counter_1_q), .up(1'b0),
    .clk(Clock_In));  // open: carry, clr
  not not_2 (not_2_out, or_1_out);
  not not_3 (not_3_out, or_1_out);
  or or_1 (or_1_out, counter_1_q[0], counter_1_q[1], counter_1_q[2], counter_1_q[3], counter_1_q[4]);
  and and_2 (Clock_Out, and_1_out, not_3_out);
endmodule

module Register_Swap (
  input  [4:0] Address_A,
  input  [4:0] Address_B,
  input  [15:0] Register_1_in,
  input  [15:0] Register_2_in,
  input  [15:0] Register_3_in,
  input  [15:0] Register_4_in,
  input  [15:0] Register_5_in,
  input  [15:0] Register_6_in,
  input  [15:0] Register_7_in,
  input  [15:0] Register_8_in,
  input  R_Swap_WE,
  input  Clock,
  output [15:0] Register_1_out,
  output [15:0] Register_2_out,
  output [15:0] Register_3_out,
  output [15:0] Register_4_out,
  output [15:0] Register_5_out,
  output [15:0] Register_6_out,
  output [15:0] Register_7_out,
  output [15:0] Register_8_out
);

  wire Eight_a_e_b, Five_a_e_b, Four_a_e_b, not_1_out, not_2_out, not_3_out, not_4_out, not_5_out, not_6_out,
       not_7_out, not_8_out, One_a_e_b, Seven_a_e_b, Six_a_e_b, Three_a_e_b, Two_a_e_b;
  wire [15:0] controlled_buffer_1_out, controlled_buffer_5_out, register_1_q, register_2_q, register_3_q,
       register_4_q, register_5_q, register_6_q, register_7_q, register_8_q;

  // Probe on Address_A
  // Probe on Address_B
  Comparator_4_bit One (
    .A(4'b0001), .B(Address_A[3:0]), .A_greater_B(1'b0), .A_equals_B(1'b1), .A_lesser_B(1'b0),
    .A_E_B(One_a_e_b));  // open: A_G_B, A_L_B
  Comparator_4_bit Two (
    .A(4'b0010), .B(Address_A[3:0]), .A_greater_B(1'b0), .A_equals_B(1'b1), .A_lesser_B(1'b0),
    .A_E_B(Two_a_e_b));  // open: A_G_B, A_L_B
  Comparator_4_bit Three (
    .A(4'b0011), .B(Address_A[3:0]), .A_greater_B(1'b0), .A_equals_B(1'b1), .A_lesser_B(1'b0),
    .A_E_B(Three_a_e_b));  // open: A_G_B, A_L_B
  Comparator_4_bit Four (
    .A(4'b0100), .B(Address_A[3:0]), .A_greater_B(1'b0), .A_equals_B(1'b1), .A_lesser_B(1'b0),
    .A_E_B(Four_a_e_b));  // open: A_G_B, A_L_B
  Comparator_4_bit Five (
    .A(4'b0101), .B(Address_B[3:0]), .A_greater_B(1'b0), .A_equals_B(1'b1), .A_lesser_B(1'b0),
    .A_E_B(Five_a_e_b));  // open: A_G_B, A_L_B
  Comparator_4_bit Six (
    .A(4'b0110), .B(Address_B[3:0]), .A_greater_B(1'b0), .A_equals_B(1'b1), .A_lesser_B(1'b0),
    .A_E_B(Six_a_e_b));  // open: A_G_B, A_L_B
  Comparator_4_bit Seven (
    .A(4'b0111), .B(Address_B[3:0]), .A_greater_B(1'b0), .A_equals_B(1'b1), .A_lesser_B(1'b0),
    .A_E_B(Seven_a_e_b));  // open: A_G_B, A_L_B
  Comparator_4_bit Eight (
    .A(4'b1000), .B(Address_B[3:0]), .A_greater_B(1'b0), .A_equals_B(1'b1), .A_lesser_B(1'b0),
    .A_E_B(Eight_a_e_b));  // open: A_G_B, A_L_B
  Register #(.width(16)) register_1 (.D(Register_1_in), .en(R_Swap_WE), .Q(register_1_q), .clk(Clock));  // open: clr
  Register #(.width(16)) register_2 (.D(Register_2_in), .en(R_Swap_WE), .Q(register_2_q), .clk(Clock));  // open: clr
  Register #(.width(16)) register_3 (.D(Register_3_in), .en(R_Swap_WE), .Q(register_3_q), .clk(Clock));  // open: clr
  Register #(.width(16)) register_4 (.D(Register_4_in), .en(R_Swap_WE), .Q(register_4_q), .clk(Clock));  // open: clr
  Register #(.width(16)) register_5 (.D(Register_5_in), .en(R_Swap_WE), .Q(register_5_q), .clk(Clock));  // open: clr
  Register #(.width(16)) register_6 (.D(Register_6_in), .en(R_Swap_WE), .Q(register_6_q), .clk(Clock));  // open: clr
  Register #(.width(16)) register_7 (.D(Register_7_in), .en(R_Swap_WE), .Q(register_7_q), .clk(Clock));  // open: clr
  Register #(.width(16)) register_8 (.D(Register_8_in), .en(R_Swap_WE), .Q(register_8_q), .clk(Clock));  // open: clr
  assign controlled_buffer_1_out = One_a_e_b ? register_1_q : 16'bz;  // Controlled_Buffer controlled_buffer_1
  assign controlled_buffer_1_out = Two_a_e_b ? register_2_q : 16'bz;  // Controlled_Buffer controlled_buffer_2
  assign controlled_buffer_1_out = Three_a_e_b ? register_3_q : 16'bz;  // Controlled_Buffer controlled_buffer_3
  assign controlled_buffer_1_out = Four_a_e_b ? register_4_q : 16'bz;  // Controlled_Buffer controlled_buffer_4
  assign controlled_buffer_5_out = Five_a_e_b ? register_5_q : 16'bz;  // Controlled_Buffer controlled_buffer_5
  assign controlled_buffer_5_out = Six_a_e_b ? register_6_q : 16'bz;  // Controlled_Buffer controlled_buffer_6
  assign controlled_buffer_5_out = Seven_a_e_b ? register_7_q : 16'bz;  // Controlled_Buffer controlled_buffer_7
  assign controlled_buffer_5_out = Eight_a_e_b ? register_8_q : 16'bz;  // Controlled_Buffer controlled_buffer_8
  // Probe on controlled_buffer_1_out
  // Probe on controlled_buffer_5_out
  assign Register_1_out = One_a_e_b ? controlled_buffer_5_out : 16'bz;  // Controlled_Buffer controlled_buffer_9
  assign Register_2_out = Two_a_e_b ? controlled_buffer_5_out : 16'bz;  // Controlled_Buffer controlled_buffer_10
  assign Register_3_out = Three_a_e_b ? controlled_buffer_5_out : 16'bz;  // Controlled_Buffer controlled_buffer_11
  assign Register_4_out = Four_a_e_b ? controlled_buffer_5_out : 16'bz;  // Controlled_Buffer controlled_buffer_12
  assign Register_5_out = Five_a_e_b ? controlled_buffer_1_out : 16'bz;  // Controlled_Buffer controlled_buffer_13
  assign Register_6_out = Six_a_e_b ? controlled_buffer_1_out : 16'bz;  // Controlled_Buffer controlled_buffer_14
  assign Register_7_out = Seven_a_e_b ? controlled_buffer_1_out : 16'bz;  // Controlled_Buffer controlled_buffer_15
  assign Register_8_out = Eight_a_e_b ? controlled_buffer_1_out : 16'bz;  // Controlled_Buffer controlled_buffer_16
  not not_1 (not_1_out, Five_a_e_b);
  not not_2 (not_2_out, Six_a_e_b);
  not not_3 (not_3_out, Seven_a_e_b);
  not not_4 (not_4_out, Eight_a_e_b);
  assign Register_5_out = not_1_out ? register_5_q : 16'bz;  // Controlled_Buffer controlled_buffer_17
  assign Register_6_out = not_2_out ? register_6_q : 16'bz;  // Controlled_Buffer controlled_buffer_18
  assign Register_7_out = not_3_out ? register_7_q : 16'bz;  // Controlled_Buffer controlled_buffer_19
  assign Register_8_out = not_4_out ? register_8_q : 16'bz;  // Controlled_Buffer controlled_buffer_20
  not not_5 (not_5_out, One_a_e_b);
  not not_6 (not_6_out, Two_a_e_b);
  not not_7 (not_7_out, Three_a_e_b);
  not not_8 (not_8_out, Four_a_e_b);
  assign Register_1_out = not_5_out ? register_1_q : 16'bz;  // Controlled_Buffer controlled_buffer_21
  assign Register_2_out = not_6_out ? register_2_q : 16'bz;  // Controlled_Buffer controlled_buffer_22
  assign Register_3_out = not_7_out ? register_3_q : 16'bz;  // Controlled_Buffer controlled_buffer_23
  assign Register_4_out = not_8_out ? register_4_q : 16'bz;  // Controlled_Buffer controlled_buffer_24
endmodule
